# Fritzing sketch barebone_ethernet_layout (saved by Fritzing 0.9.3b)
circuit board: 3.4cm x 7.5cm
breadboards: 3

parts:
  A1 = olimex ESP32-POE-ISO
  Bauteil1 = TXB0108 8-channel Bi-directional Logic Level Converter
  R1 = Resistor [tolerance=±5% resistance=10k package=THT]
  U1 = MAX485 [package=dil08]

nets:
  N1: A1.Pin_1, Bauteil1.VCCB, U1.VCC
  N2: A1.Pin_2, A1.Pin_31, Bauteil1.VCCA, R1.Pin_1
  GND: A1.Pin_3, Bauteil1.GND, U1.GND
  N3: A1.Pin_16, Bauteil1.A6
  N4: A1.Pin_17, Bauteil1.A5
  N5: A1.Pin_18, Bauteil1.A4
  N6: Bauteil1.B4, U1.RO
  N7: Bauteil1.B5, U1.RE, U1.DE
  N8: Bauteil1.B6, U1.DI
  N9: Bauteil1.OE, R1.Pin_0

custom parts:
  olimex ESP32-POE-ISO: ESP32-PoE is an IoT WIFI/BLE/Ethernet development board with Power-Over-Ethernet feature.
  TXB0108 8-channel Bi-directional Logic Level Converter: Because the Arduino (and Basic Stamp) are 5V devices, and most modern sensors, displays, flash cards and modes are 3.3V-only, many makers find that they need to perform level shifting/conversion to protect the 3.3V device from 5V. Although one can use resistors to make a divider, for high speed transfers, the resistors can add a lot of slew and cause havoc that is tough to debug. For that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
